// Logisim project hw3.circ as structural Verilog: 3 circuits, main circuit carry
module carry (
  input  in_1,
  input  in_2,
  input  in_3,
  output out_4,
  output out_5
);

  wire and_2_out, or_1_out, or_2_out, xor_1_out;

  and and_1 (out_4, or_1_out, or_2_out);
  or or_1 (or_1_out, in_1, in_2);
  and and_2 (and_2_out, in_1, in_2);
  or or_2 (or_2_out, and_2_out, in_3);
  xor xor_1 (xor_1_out, in_1, in_2);
  xor xor_2 (out_5, in_3, xor_1_out);
endmodule

module adder (
  input  [3:0] A,
  input  [3:0] B,
  input  in_3,
  input  [3:0] in_4,
  output out_5
);

  wire carry_2_out_4, carry_3_out_4, carry_4_out_4;

  carry carry_1 (.out_4(out_5), .in_1(A[3]), .in_2(B[3]), .out_5(in_4[3]), .in_3(carry_2_out_4));
  carry carry_2 (.out_4(carry_2_out_4), .in_1(A[2]), .in_2(B[2]), .out_5(in_4[2]), .in_3(carry_3_out_4));
  carry carry_3 (.out_4(carry_3_out_4), .in_1(A[1]), .in_2(A[1]), .out_5(in_4[1]), .in_3(carry_4_out_4));
  carry carry_4 (.out_4(carry_4_out_4), .in_1(A[0]), .in_2(B[0]), .out_5(in_4[0]), .in_3(in_3));

  assign B[1] = A[1];

  // Other names for the same wires on the sheet: B1 = A[1]
endmodule

module alu (
  input  [3:0] in_1,
  input  [3:0] in_2,
  input  [2:0] in_3,
  input  in_4,
  output out_5,
  output [3:0] out_6,
  output [3:0] out_7
);

  wire [3:0] undriven;

  adder adder_1 (.out_5(out_5), .A(in_1), .B(in_2), .in_4(out_7), .in_3(in_4));
  Multiplexer #(.select(3), .width(4), .disabled(0), .enable("false")) multiplexer_1 (
    .in0(undriven), .out(out_6), .sel(in_3));  // open: in1, in2, in3, in4, in5, in6, in7
endmodule
